# Fritzing sketch Riego v2.0 (saved by Fritzing 0.9.3b)
breadboards: 2

parts:
  Arduino_Uno_v3 = Arduino Uno (Rev3)
  Bateria_de_plomo = 12 battery [package=battery]
  Sensor_ultrasónico = HC-SR04 Ultrasonic Distance Sensor
  Reloj_RTC = ZS-042 RTC Module
  Panel_solar_12V = Solar Panel [package="Renogy 10Watts 12 Volt Monocrystalline Bendable Solar Panel"]
  Bomba_1 = water pump/motor
  Bomba_2 = water pump/motor
  Relé_de_4_canales = 4 channel relay module [package=THT]
  Sensor_humedad_tierra4 = DFRobot Capacitive Soil Moisture Sensor V1.0 [part_number=SEN0193]
  LCD_I2C = LCD1602-I2C
  Módulo_de_carga = solar charger MPPT 1A
  Sensor_humedad_tierra1 = DFRobot Capacitive Soil Moisture Sensor V1.0 [part_number=SEN0193]
  Sensor_humedad_tierra2 = DFRobot Capacitive Soil Moisture Sensor V1.0 [part_number=SEN0193]
  Sensor_humedad_tierra3 = DFRobot Capacitive Soil Moisture Sensor V1.0 [part_number=SEN0193]
  Sensor_humedad_y_temperatura = Humidity Sensor - HIH-4030 Breakout
  Sensor_de_potencia_lumínica = BH1750
  Bomba_3 = water pump/motor
  Bomba_4 = water pump/motor
  Regulador_de_potencia_5V = Voltage Regulator LM1117 [package=sot223]

nets:
  N1: Arduino_Uno_v3.A0, Sensor_humedad_tierra1.A
  N2: Arduino_Uno_v3.A1, Sensor_humedad_tierra2.A
  N3: Arduino_Uno_v3.A2, Sensor_humedad_tierra4.A
  N4: Arduino_Uno_v3.A3, Sensor_humedad_tierra3.A
  N5: Arduino_Uno_v3.A4/SDA, Arduino_Uno_v3.A5/SCL, Reloj_RTC.SDA, Reloj_RTC.SCL, LCD_I2C.SDA, LCD_I2C.SCL, Sensor_de_potencia_lumínica.SCL, Sensor_de_potencia_lumínica.SDA
  N6: Arduino_Uno_v3.D8, Relé_de_4_canales.Pin_27
  N7: Arduino_Uno_v3.D10_PWM/SS, Sensor_ultrasónico.TRIG
  N8: Arduino_Uno_v3.D11_PWM/MOSI, Sensor_ultrasónico.ECHO
  N9: Arduino_Uno_v3.D12/MISO, Sensor_humedad_y_temperatura.OUT
  GND: Arduino_Uno_v3.GND, Sensor_ultrasónico.GND, Reloj_RTC.GND, Relé_de_4_canales.Pin_26, Sensor_humedad_tierra4.GND, LCD_I2C.GND, Sensor_humedad_tierra1.GND, Sensor_humedad_tierra2.GND, Sensor_humedad_tierra3.GND, Sensor_humedad_y_temperatura.GND, Sensor_de_potencia_lumínica.GND, Regulador_de_potencia_5V.IN
  N10: Arduino_Uno_v3.D5_PWM, Relé_de_4_canales.Pin_30
  N11: Arduino_Uno_v3.D6_PWM, Relé_de_4_canales.Pin_29
  N12: Arduino_Uno_v3.D7, Relé_de_4_canales.Pin_28
  VCC: Arduino_Uno_v3.3V3, Reloj_RTC.VCC, Sensor_humedad_tierra4.VCC, LCD_I2C.VCC, Sensor_humedad_tierra1.VCC, Sensor_humedad_tierra2.VCC, Sensor_humedad_tierra3.VCC, Sensor_de_potencia_lumínica.VCC
  VCC_2: Arduino_Uno_v3.5V, Sensor_ultrasónico.VCC, Relé_de_4_canales.Pin_25, Sensor_humedad_y_temperatura.VCC
  N13: Arduino_Uno_v3.VIN, Bateria_de_plomo.-, Bomba_1.pin_1, Bomba_2.pin_1, Módulo_de_carga.Pin_4, Bomba_3.pin_1, Bomba_4.pin_1, Regulador_de_potencia_5V.OUT
  N14: Bateria_de_plomo.+, Panel_solar_12V.Connector_2, Módulo_de_carga.Pin_2, Módulo_de_carga.Pin_3, Regulador_de_potencia_5V.ADJ
  N15: Panel_solar_12V.Connector_1, Módulo_de_carga.Pin_1
  N16: Bomba_1.pin_2, Relé_de_4_canales.Pin_11
  N17: Bomba_2.pin_2, Relé_de_4_canales.Pin_8
  N18: Relé_de_4_canales.Pin_2, Bomba_4.pin_2
  N19: Relé_de_4_canales.Pin_5, Bomba_3.pin_2

custom parts:
  12 battery: 12V lead acid type battery, like the Husqvarna YTH2448 12V 35AH battery. This is the mini version 1/4 the size of the actual battery to be closer to typical breadboard parts (around 2in wide rathher than 7in). The pads in pcb are sized to accomidate up to 14ga wire (as these batterys will deliver high currents.)
  Solar Panel: 10 W 12 V
  water pump/motor: WATER PUMP BY ARDUBLOCKTR
  4 channel relay module: 4 channel Relay Module 5V 12V 24V High and Low Level Trigger Relay Control With Optocoupler Two Way relays DC 5 V 12 V 24 V Volt.
  DFRobot Capacitive Soil Moisture Sensor V1.0: DFRobot Capacitive Soil Moisture Sensor V1.0 This product measures soil moisture levels by capacitive sensing, rather than resistive sensing like other types of moisture sensor. It is made of a corrosion resistant material giving it a long service life. Insert it into soil and impress your friends with the real-time soil moisture data! The product includes an on-board voltage regulator which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
  LCD1602-I2C: A standard character display, usually with 2x16 characters. Comes in many colors with LCM1602 IIC attached.
  solar charger MPPT 1A: controlador de carga MPPT
  BH1750: Light Sensor

// code stored in the sketch: waterin1.ino

const int relayPin = 8;
const int sensor_pin = A0; // Soil Sensor input at Analog PIN A0
int output_value;

void setup() {
  Serial.begin(9600);                  
  pinMode(relayPin, OUTPUT);
  pinMode(sensor_pin, INPUT);
  Serial.println("Reading From the Sensor ...");
  delay(2000);
}

void loop() {
  output_value = analogRead(sensor_pin);
  output_value = map(output_value, 550, 10, 0, 100);
  
  Serial.print("Moisture: ");
  Serial.print(output_value);
  Serial.println("%");
  
  if (output_value < 20) {
    digitalWrite(relayPin, LOW);  // Turn pump ON when soil is dry
    Serial.println("Pump ON");
  } else {
    digitalWrite(relayPin, HIGH);   // Turn pump OFF when soil is moist
    Serial.println("Pump OFF");
  }
  
  delay(3000);
}
