# Fritzing sketch Riego v2.1 (saved by Fritzing 0.9.3b)

parts:
  Arduino_Uno_v3 = Arduino Uno (Rev3)
  Bateria_de_plomo = 12 battery [package=battery]
  Sensor_ultrasónico = HC-SR04 Ultrasonic Distance Sensor
  Reloj_RTC = ZS-042 RTC Module
  Panel_solar_12V = Solar Panel [package="Renogy 10Watts 12 Volt Monocrystalline Bendable Solar Panel"]
  Bomba_1 = water pump/motor
  Bomba_2 = water pump/motor
  Relé_de_4_canales = 4 channel relay module [package=THT]
  Sensor_humedad_tierra4 = DFRobot Capacitive Soil Moisture Sensor V1.0 [part_number=SEN0193]
  LCD_I2C = LCD1602-I2C
  Módulo_de_carga = solar charger MPPT 1A
  Sensor_humedad_tierra1 = DFRobot Capacitive Soil Moisture Sensor V1.0 [part_number=SEN0193]
  Sensor_humedad_tierra2 = DFRobot Capacitive Soil Moisture Sensor V1.0 [part_number=SEN0193]
  Sensor_humedad_tierra3 = DFRobot Capacitive Soil Moisture Sensor V1.0 [part_number=SEN0193]
  Sensor_humedad_y_temperatura = Humidity Sensor - HIH-4030 Breakout
  Sensor_de_potencia_lumínica = BH1750  # not connected
  Bomba_3 = water pump/motor
  Bomba_4 = water pump/motor
  Regulador_de_potencia_5V = Voltage Regulator LM1117 [package=sot223]

nets:
  N1: Arduino_Uno_v3.A0, Sensor_humedad_tierra1.A
  N2: Arduino_Uno_v3.A1, Sensor_humedad_tierra2.A
  N3: Arduino_Uno_v3.A2, Sensor_humedad_tierra4.A
  N4: Arduino_Uno_v3.A3, Sensor_humedad_tierra3.A
  N5: Arduino_Uno_v3.A4/SDA, Arduino_Uno_v3.A5/SCL, Reloj_RTC.SDA, Reloj_RTC.SCL, LCD_I2C.SDA, LCD_I2C.SCL
  N6: Arduino_Uno_v3.D8, Relé_de_4_canales.Pin_27
  N7: Arduino_Uno_v3.D10_PWM/SS, Sensor_ultrasónico.TRIG
  N8: Arduino_Uno_v3.D11_PWM/MOSI, Sensor_ultrasónico.ECHO
  N9: Arduino_Uno_v3.D12/MISO, Sensor_humedad_y_temperatura.OUT
  GND: Arduino_Uno_v3.GND, Sensor_ultrasónico.GND, Reloj_RTC.GND, Relé_de_4_canales.Pin_26, Sensor_humedad_tierra4.GND, LCD_I2C.GND, Sensor_humedad_tierra1.GND, Sensor_humedad_tierra2.GND, Sensor_humedad_tierra3.GND, Sensor_humedad_y_temperatura.GND, Regulador_de_potencia_5V.IN
  N10: Arduino_Uno_v3.D5_PWM, Relé_de_4_canales.Pin_30
  N11: Arduino_Uno_v3.D6_PWM, Relé_de_4_canales.Pin_29
  N12: Arduino_Uno_v3.D7, Relé_de_4_canales.Pin_28
  VCC: Arduino_Uno_v3.3V3, Reloj_RTC.VCC, Sensor_humedad_tierra4.VCC, Sensor_humedad_tierra1.VCC, Sensor_humedad_tierra2.VCC, Sensor_humedad_tierra3.VCC
  VCC_2: Arduino_Uno_v3.5V, Sensor_ultrasónico.VCC, Relé_de_4_canales.Pin_25, LCD_I2C.VCC, Sensor_humedad_y_temperatura.VCC
  N13: Arduino_Uno_v3.VIN, Bateria_de_plomo.-, Bomba_1.pin_1, Bomba_2.pin_1, Módulo_de_carga.Pin_4, Bomba_3.pin_1, Bomba_4.pin_1, Regulador_de_potencia_5V.OUT
  N14: Bateria_de_plomo.+, Panel_solar_12V.Connector_2, Módulo_de_carga.Pin_2, Módulo_de_carga.Pin_3, Regulador_de_potencia_5V.ADJ
  N15: Panel_solar_12V.Connector_1, Módulo_de_carga.Pin_1
  N16: Bomba_1.pin_2, Relé_de_4_canales.Pin_11
  N17: Bomba_2.pin_2, Relé_de_4_canales.Pin_8
  N18: Relé_de_4_canales.Pin_2, Bomba_4.pin_2
  N19: Relé_de_4_canales.Pin_5, Bomba_3.pin_2

notes:
  Sensor de luminosidad no funciona comprar otro o reparar

custom parts:
  12 battery: 12V lead acid type battery, like the Husqvarna YTH2448 12V 35AH battery. This is the mini version 1/4 the size of the actual battery to be closer to typical breadboard parts (around 2in wide rathher than 7in). The pads in pcb are sized to accomidate up to 14ga wire (as these batterys will deliver high currents.)
  Solar Panel: 10 W 12 V
  water pump/motor: WATER PUMP BY ARDUBLOCKTR
  4 channel relay module: 4 channel Relay Module 5V 12V 24V High and Low Level Trigger Relay Control With Optocoupler Two Way relays DC 5 V 12 V 24 V Volt.
  DFRobot Capacitive Soil Moisture Sensor V1.0: DFRobot Capacitive Soil Moisture Sensor V1.0 This product measures soil moisture levels by capacitive sensing, rather than resistive sensing like other types of moisture sensor. It is made of a corrosion resistant material giving it a long service life. Insert it into soil and impress your friends with the real-time soil moisture data! The product includes an on-board voltage regulator which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
  LCD1602-I2C: A standard character display, usually with 2x16 characters. Comes in many colors with LCM1602 IIC attached.
  solar charger MPPT 1A: controlador de carga MPPT
  BH1750: Light Sensor

// code stored in the sketch: waterin1.ino

const int relayPin = 8;
const int sensor_pin = A0; // Soil Sensor input at Analog PIN A0
int output_value;

void setup() {
  Serial.begin(9600);                  
  pinMode(relayPin, OUTPUT);
  pinMode(sensor_pin, INPUT);
  Serial.println("Reading From the Sensor ...");
  delay(2000);
}

void loop() {
  output_value = analogRead(sensor_pin);
  output_value = map(output_value, 550, 10, 0, 100);
  
  Serial.print("Moisture: ");
  Serial.print(output_value);
  Serial.println("%");
  
  if (output_value < 20) {
    digitalWrite(relayPin, LOW);  // Turn pump ON when soil is dry
    Serial.println("Pump ON");
  } else {
    digitalWrite(relayPin, HIGH);   // Turn pump OFF when soil is moist
    Serial.println("Pump OFF");
  }
  
  delay(3000);
}

// code stored in the sketch: Watering2.0.ino
#include <Wire.h>
#include <LiquidCrystal_I2C.h>
#include <DHT.h>
#include <RTClib.h>
#include <EEPROM.h>


LiquidCrystal_I2C lcd(0x27, 16, 2); // Dirección I2C 0x27, 16 columnas y 2 filas
RTC_DS3231 rtc;



const float MAX_TEMPERATURE = 34.0; // Maximum temperature threshold in Celsius
const int relayPin = 8;
const int sensor_pin = A0; // Soil Sensor input at Analog PIN A0
const int DHTPIN = 12;     // DHT sensor
const int TRIGGER_PIN = 11;
const int ECHO_PIN = 10;


#define DHTTYPE DHT22   // DHT 22  (AM2302)
DHT dht(DHTPIN, DHTTYPE);


#define TIME_SET_FLAG_ADDRESS 0


int output_value;
float humidity, temperature;
long duration;
int distanceCm;


void setup() 
{
  Serial.begin(9600);
  Wire.begin();  // Inicializa I2C
    Serial.println("I2C Scanner");
  byte error, address;
  int nDevices;
  nDevices = 0;
  for(address = 1; address < 127; address++ ) {
    Wire.beginTransmission(address);
    error = Wire.endTransmission();
    if (error == 0) {
      Serial.print("I2C device found at address 0x");
      if (address<16) {
        Serial.print("0");
      }
      Serial.println(address,HEX);
      nDevices++;
    }
  }
  if (nDevices == 0) {
    Serial.println("No I2C devices found\n");
  }
  else {
    Serial.println("done\n");
  }


  pinMode(relayPin, OUTPUT);
  pinMode(sensor_pin, INPUT);
  pinMode(TRIGGER_PIN, OUTPUT);
  pinMode(ECHO_PIN, INPUT);
  
  dht.begin();


  if (!rtc.begin()) {
    Serial.println("Couldn't find RTC");
    while (1);
  }


  // Check if RTC time has been set before
  byte timeSetFlag = EEPROM.read(TIME_SET_FLAG_ADDRESS);


  if (timeSetFlag != 1) {
    // Time hasn't been set, so set it now
    rtc.adjust(DateTime(F(__DATE__), F(__TIME__)));
    
    // Set the flag in EEPROM
    EEPROM.write(TIME_SET_FLAG_ADDRESS, 1);
    
    Serial.println("RTC time set to compilation time.");
  } else {
    Serial.println("RTC time already set.");
  }


  
  lcd.init();   // Inicializa el LCD
  lcd.backlight();
  
  Serial.println("Reading From the Sensor ...");
  delay(2000);
}


void loop() {
  DateTime now = rtc.now();
  
  // Leer sensor de humedad del suelo
  output_value = analogRead(sensor_pin);
  output_value = map(output_value, 550, 10, 0, 100);
  
  // Leer DHT sensor
  humidity = dht.readHumidity();
  temperature = dht.readTemperature();
  
  // Leer sensor ultrasónico
  digitalWrite(TRIGGER_PIN, LOW);
  delayMicroseconds(2);
  digitalWrite(TRIGGER_PIN, HIGH);
  delayMicroseconds(10);
  digitalWrite(TRIGGER_PIN, LOW);
  duration = pulseIn(ECHO_PIN, HIGH);
  distanceCm = duration * 0.034 / 2;
  
  // Control de la bomba
  bool shouldPump = false;
  
  if (output_value < 20) {  // Check if soil is dry
    if (temperature < 34.0) {  // Check temperature condition
      int currentMonth = now.month();
      int currentHour = now.hour();
      
      if (currentMonth >= 6 && currentMonth <= 9) {  // June to September
        if (currentHour < 11 || currentHour >= 20) {
          shouldPump = true;
        }
      } else {  // Other months
        if (currentHour < 12 || currentHour >= 18) {
          shouldPump = true;
        }
      }
    }
  }
  
  if (shouldPump) {
    digitalWrite(relayPin, LOW);  // Turn pump ON
  } else {
    digitalWrite(relayPin, HIGH);  // Turn pump OFF
  }
  
  
  updateLCD(now);
  printSerial(now);
  
  delay(3000);
}


void updateLCD(DateTime now) {
  lcd.clear();
  
  // First row
  lcd.setCursor(0, 0);
  if (now.day() < 10) lcd.print('0');
  lcd.print(now.day());
  lcd.print('/');
  if (now.month() < 10) lcd.print('0');
  lcd.print(now.month());


  lcd.setCursor(6, 0);
  if (now.hour() < 10) lcd.print('0');
  lcd.print(now.hour(), DEC);
  lcd.print(':');
  if (now.minute() < 10) lcd.print('0');
  lcd.print(now.minute(), DEC);
  
  lcd.setCursor(12, 0);
  lcd.print("T:");
  int tempInt = (int)temperature;
  if (tempInt < 10) lcd.print('0');
  lcd.print(tempInt);
  lcd.print("C");
  
  // Second row
  lcd.setCursor(0, 1);
  lcd.print("S:");
  lcd.print(output_value);
  lcd.print("%");


  lcd.setCursor(6, 1);
  lcd.print("W:");
  int waterLevel = 100 - map(distanceCm, 0, 20, 0, 100); // Assuming 20cm is the max depth
  waterLevel = constrain(waterLevel, 0, 99); // Ensure it's between 0 and 99
  if (waterLevel < 10) lcd.print('0');
  lcd.print(waterLevel);
  lcd.print("%");
  
  lcd.setCursor(12, 1);
  lcd.print("P:");
  lcd.print(digitalRead(relayPin) == LOW ? "ON" : "NO");
}


void printSerial(DateTime now) {
  Serial.print(now.year(), DEC);
  Serial.print('/');
  Serial.print(now.month(), DEC);
  Serial.print('/');
  Serial.print(now.day(), DEC);
  Serial.print(" ");
  Serial.print(now.hour(), DEC);
  Serial.print(':');
  Serial.print(now.minute(), DEC);
  Serial.print(':');
  Serial.print(now.second(), DEC);
  Serial.println();


  Serial.print("Soil Moisture: ");
  Serial.print(output_value);
  Serial.println("%");
  
  Serial.print("Water Level: ");
  Serial.print(distanceCm);
  Serial.println(" cm");
  
  Serial.print("Temperature: ");
  Serial.print(temperature);
  Serial.println(" C");


  Serial.print("Humidity: ");
  Serial.print(humidity);
  Serial.println("%");
  
  Serial.println(digitalRead(relayPin) == LOW ? "Pump ON" : "Pump OFF");
  Serial.println();
}
